# Fritzing sketch ESP8266 (saved by Fritzing 0.9.2b)
breadboards: 1

parts:
  U1 = ESP8266 WiFi Module [part_number=ESP8266]
  C2 = Electrolytic Capacitor [capacitance=10µF voltage=10V package="100 mil [THT, electrolytic]"]
  C1 = Ceramic Capacitor [capacitance=100nF voltage=10V package="100 mil [THT, multilayer]"]
  IR1 = TSOP312.., 314.. [package=THT]
  U2 = V_REG_LD1117VXX [package=78xxl]
  D1 = LTE-302 [package=lte-302]
  U3 = SWITCH_SPDT [package=kps-1290]
  R1 = Resistor [tolerance=±5% resistance=22 package=THT]
  S1 = Pushbutton [package="[SMD]"]

nets:
  N1: U1.VCC, U1.CH_PD, C2.+, IR1.Vs, U2.OUT, R1.Pin_0
  N2: U1.GPIO_0, U3.P
  N3: U1.RST, S1.Pin_1, S1.Pin_2
  N4: U1.GPIO_2, IR1.Data
  GND: U1.GND, C2.-, C1.0, IR1.GND, U2.GND, U3.S, S1.Pin_3, S1.Pin_4
  5V: C1.1, U2.IN
  N5: D1.A, R1.Pin_1
  N6: D1.C, U3.O

custom parts:
  ESP8266 WiFi Module: Generic WiFi Module based on the ESP8266 with onboard PCB antenna and UART communications
